# Fritzing sketch Musical Inst. Schematic (saved by Fritzing 0.9.3b)
circuit board: 8.46667cm x 5.64444cm
breadboards: 1

parts:
  Musical_Instrument = Arduino Uno (Rev3)
  R4 = Resistor [tolerance=±5% resistance=10k package=THT]
  R3 = Resistor [tolerance=±5% resistance=10k package=THT]
  R2 = Resistor [tolerance=±5% resistance=10k package=THT]
  R1 = Resistor [tolerance=±5% resistance=10k package=THT]
  S4 = Pushbutton [package="[THT]"]
  S3 = Pushbutton [package="[THT]"]
  S2 = Pushbutton [package="[THT]"]
  S1 = Pushbutton [package="[THT]"]

nets:
  N1: Musical_Instrument.GND, R4.Pin_1, R3.Pin_1, R2.Pin_1, R1.Pin_1
  N2: Musical_Instrument.D2, R1.Pin_0, S1.Pin_1, S1.Pin_2
  N3: Musical_Instrument.D3_PWM, R2.Pin_0, S2.Pin_1, S2.Pin_2
  N4: Musical_Instrument.D4, R3.Pin_0, S3.Pin_1, S3.Pin_2
  N5: Musical_Instrument.D5_PWM, R4.Pin_0, S4.Pin_1, S4.Pin_2
  N6: Musical_Instrument.5V, S4.Pin_3, S4.Pin_4, S3.Pin_3, S3.Pin_4, S2.Pin_3, S2.Pin_4, S1.Pin_4
